// Logisim project 1235813_counter_viva.circ as structural Verilog: 3 circuits, main circuit main
module main (
  output [3:0] out_1
);

  wire _2_qn, _3_qn, _4_qn, and_1_out_3, and_2_out_3, and_3_out_3, clock_1_out, or_1_out_3;

  Clock clock_1 (.out(clock_1_out));
  J_K_Flip_Flop _4 (
    .J(out_1[2]), .clk(clock_1_out), .K(out_1[2]), .Q(out_1[3]), .Qn(_4_qn));  // open: preset, en, reset
  OR or_1 (.in_1(out_1[3]), .in_2(and_2_out_3), .out_3(or_1_out_3));
  J_K_Flip_Flop _3 (.J(or_1_out_3), .clk(clock_1_out), .K(1'b1), .Q(out_1[2]), .Qn(_3_qn));  // open: preset, en, reset
  AND and_1 (.in_1(_3_qn), .in_2(_4_qn), .out_3(and_1_out_3));
  AND and_2 (.in_1(out_1[1]), .in_2(out_1[0]), .out_3(and_2_out_3));
  J_K_Flip_Flop _2 (
    .J(and_1_out_3), .clk(clock_1_out), .K(out_1[0]), .Q(out_1[1]), .Qn(_2_qn));  // open: preset, en, reset
  AND and_3 (.in_1(_2_qn), .in_2(_4_qn), .out_3(and_3_out_3));
  J_K_Flip_Flop _1 (.J(1'b1), .clk(clock_1_out), .K(and_3_out_3), .Q(out_1[0]));  // open: Qn, preset, en, reset
endmodule

module OR (
  input  in_1,
  input  in_2,
  output out_3
);

  wire nand_1_out, nand_2_out;

  nand nand_1 (nand_1_out, in_1, in_1);
  nand nand_2 (nand_2_out, in_2, in_2);
  nand nand_3 (out_3, nand_1_out, nand_2_out);
endmodule

module AND (
  input  in_1,
  input  in_2,
  output out_3
);

  wire nand_1_out;

  nand nand_1 (nand_1_out, in_1, in_2);
  nand nand_2 (out_3, nand_1_out, nand_1_out);
endmodule
