// Logisim project 2-bit adder.circ as structural Verilog: 1 circuit, main circuit main
module main (
  input  A1,
  input  B1,
  input  A0,
  input  B0,
  output S0,
  output S1,
  output S2
);

  wire nand_1_out, nand_2_out, nand_3_out, nand_4_out, xor_2_out;

  xor xor_1 (S0, A0, B0);
  nand nand_1 (nand_1_out, B0, A0);
  not nand_2 (nand_2_out, nand_1_out);  // NAND_Gate
  xor xor_2 (xor_2_out, B1, A1);
  nand nand_3 (nand_3_out, B1, A1);
  xor xor_3 (S1, xor_2_out, nand_2_out);
  nand nand_4 (nand_4_out, xor_2_out, nand_2_out);
  nand nand_5 (S2, nand_4_out, nand_3_out);
endmodule
