// Logisim project BCD to X3.circ as structural Verilog: 1 circuit, main circuit main
module main (
  input  _0,
  input  _1,
  input  A,
  input  [2:0] BCD,
  output E0,
  output E1,
  output E2,
  output E3
);

  wire A_prime_out;

  not A_prime (A_prime_out, A);
  Multiplexer #(.select(3), .enable("false")) multiplexer_1 (
    .in0(A), .in1(A), .in2(_0), .in3(_0), .in4(_0), .in5(_1), .in6(_1), .in7(_1), .out(E0), .sel(BCD));
  Multiplexer #(.select(3), .enable("false")) multiplexer_2 (
    .in0(_0), .in1(_1), .in2(_1), .in3(_1), .in4(_1), .in5(_0), .in6(_0), .in7(_0), .out(E1), .sel(BCD));
  Multiplexer #(.select(3), .enable("false")) multiplexer_3 (
    .in0(_1), .in1(_0), .in2(_0), .in3(_1), .in4(_1), .in5(_0), .in6(_0), .in7(_1), .out(E2), .sel(BCD));
  Multiplexer #(.select(3), .enable("false")) multiplexer_4 (
    .in0(_1), .in1(_0), .in2(_1), .in3(_0), .in4(_1), .in5(_0), .in6(_1), .in7(_0), .out(E3), .sel(BCD));
endmodule
