// Logisim project DECADE2.circ as structural Verilog: 1 circuit, main circuit main
module main (
  input  S,
  output [3:0] out_2
);

  wire and_1_out, and_2_out, and_3_out, and_4_out, and_5_out, and_6_out, and_7_out, and_8_out, and_9_out,
       and_10_out, and_11_out, Clear_out, clock_1_out, j_k_ff_1_qn, j_k_ff_2_qn, j_k_ff_3_qn, j_k_ff_4_qn,
       multiplexer_1_out, multiplexer_2_out, multiplexer_3_out, or_1_out, or_2_out, or_3_out;

  Clock clock_1 (.out(clock_1_out));
  Button Clear (.out(Clear_out));
  J_K_Flip_Flop j_k_ff_1 (
    .J(1'b1), .clk(clock_1_out), .K(1'b1), .Q(out_2[0]), .Qn(j_k_ff_1_qn), .reset(Clear_out));  // open: preset, en
  and and_1 (and_1_out, out_2[0], j_k_ff_4_qn);
  and and_2 (and_2_out, out_2[1], j_k_ff_1_qn);
  and and_3 (and_3_out, out_2[2], j_k_ff_1_qn);
  and and_4 (and_4_out, out_2[3], j_k_ff_1_qn);
  or or_1 (or_1_out, and_2_out, and_3_out, and_4_out);
  J_K_Flip_Flop j_k_ff_2 (
    .J(multiplexer_1_out), .clk(clock_1_out), .K(multiplexer_1_out), .Q(out_2[1]), .Qn(j_k_ff_2_qn),
    .reset(Clear_out));  // open: preset, en
  Multiplexer #(.enable("false")) multiplexer_1 (.in0(and_1_out), .in1(or_1_out), .out(multiplexer_1_out), .sel(S));
  and and_5 (and_5_out, out_2[0], out_2[1]);
  and and_6 (and_6_out, j_k_ff_2_qn, j_k_ff_1_qn);
  and and_7 (and_7_out, out_2[2], and_6_out);
  and and_8 (and_8_out, and_6_out, out_2[3]);
  Multiplexer #(.enable("false")) multiplexer_2 (.in0(and_5_out), .in1(or_2_out), .out(multiplexer_2_out), .sel(S));
  or or_2 (or_2_out, and_7_out, and_8_out);
  J_K_Flip_Flop j_k_ff_3 (
    .J(multiplexer_2_out), .clk(clock_1_out), .K(multiplexer_2_out), .Q(out_2[2]), .Qn(j_k_ff_3_qn),
    .reset(Clear_out));  // open: preset, en
  and and_9 (and_9_out, and_5_out, out_2[2]);
  or or_3 (or_3_out, and_9_out, and_10_out);
  and and_10 (and_10_out, out_2[0], out_2[3]);
  Hex_Digit_Display hex_digit_display_1 (.value(out_2));  // open: dp
  Multiplexer #(.enable("false")) multiplexer_3 (.in0(or_3_out), .in1(and_11_out), .out(multiplexer_3_out), .sel(S));
  and and_11 (and_11_out, j_k_ff_3_qn, j_k_ff_2_qn, j_k_ff_1_qn);
  J_K_Flip_Flop j_k_ff_4 (
    .J(multiplexer_3_out), .clk(clock_1_out), .K(multiplexer_3_out), .Q(out_2[3]), .Qn(j_k_ff_4_qn),
    .reset(Clear_out));  // open: preset, en
endmodule
