// Logisim project Decimal_to_BCD.circ as structural Verilog: 1 circuit, main circuit main
module main (
  input  I0,
  input  I1,
  input  I2,
  input  I3,
  input  I4,
  input  I5,
  input  I6,
  input  I7,
  input  I8,
  input  I9,
  output out_11,
  output out_12,
  output out_13,
  output out_14
);

  or B0 (out_11, I1, I3, I9, I7, I5);
  or B1 (out_12, I2, I3, I7, I6);
  or B2 (out_13, I5, I4, I6, I7);
  or B3 (out_14, I8, I9);
endmodule
