// Logisim project HHMMSS.circ as structural Verilog: 5 circuits, main circuit main
module main (
  input  in_1,
  input  Clear,
  output [3:0] out_3
);

  wire and_1_out, and_2_out, and_3_out, and_4_out, j_k_ff_4_qn, or_1_out;

  and and_1 (and_1_out, out_3[0], j_k_ff_4_qn);
  J_K_Flip_Flop j_k_ff_1 (.J(1'b1), .clk(in_1), .K(1'b1), .Q(out_3[0]), .reset(Clear));  // open: Qn, preset, en
  J_K_Flip_Flop j_k_ff_2 (
    .J(and_1_out), .clk(in_1), .K(and_1_out), .Q(out_3[1]), .reset(Clear));  // open: Qn, preset, en
  and and_2 (and_2_out, out_3[0], out_3[1]);
  J_K_Flip_Flop j_k_ff_3 (
    .J(and_2_out), .clk(in_1), .K(and_2_out), .Q(out_3[2]), .reset(Clear));  // open: Qn, preset, en
  and and_3 (and_3_out, and_2_out, out_3[2]);
  or or_1 (or_1_out, and_3_out, and_4_out);
  and and_4 (and_4_out, out_3[0], out_3[3]);
  J_K_Flip_Flop j_k_ff_4 (
    .J(or_1_out), .clk(in_1), .K(or_1_out), .Q(out_3[3]), .Qn(j_k_ff_4_qn), .reset(Clear));  // open: preset, en
endmodule

module counter6 (
  input  in_1,
  input  Clear,
  output [2:0] out_3
);

  wire and_1_out, and_2_out, and_3_out, j_k_ff_3_qn, or_1_out;

  J_K_Flip_Flop j_k_ff_1 (.J(1'b1), .clk(in_1), .K(1'b1), .Q(out_3[0]), .reset(Clear));  // open: Qn, preset, en
  J_K_Flip_Flop j_k_ff_2 (
    .J(and_1_out), .clk(in_1), .K(and_1_out), .Q(out_3[1]), .reset(Clear));  // open: Qn, preset, en
  and and_1 (and_1_out, j_k_ff_3_qn, out_3[0]);
  and and_2 (and_2_out, out_3[2], out_3[0]);
  and and_3 (and_3_out, out_3[0], out_3[1]);
  or or_1 (or_1_out, and_2_out, and_3_out);
  J_K_Flip_Flop j_k_ff_3 (
    .J(or_1_out), .clk(in_1), .K(or_1_out), .Q(out_3[2]), .Qn(j_k_ff_3_qn), .reset(Clear));  // open: preset, en
endmodule

module s (
  input  in_1,
  input  in_2,
  output [3:0] Z,
  output [3:0] T
);

  wire and_1_out, not_1_out, not_2_out, not_3_out, not_4_out;

  main main_1 (.in_1(in_1), .Clear(in_2), .out_3(Z));
  not not_1 (not_1_out, Z[1]);
  not not_2 (not_2_out, Z[2]);
  not not_3 (not_3_out, Z[0]);
  not not_4 (not_4_out, Z[3]);
  counter6 counter6_1 (.in_1(and_1_out), .Clear(in_2), .out_3(T[2:0]));
  and and_1 (and_1_out, not_3_out, not_1_out, not_2_out, not_4_out);

  assign T[3] = 1'b0;
endmodule

module counter24 (
  input  in_1,
  input  Clear,
  output [4:0] out_3
);

  wire and_1_out, and_2_out, and_3_out, j_k_ff_5_qn, xor_1_out;

  J_K_Flip_Flop j_k_ff_1 (.J(1'b1), .clk(in_1), .K(1'b1), .Q(out_3[0]), .reset(Clear));  // open: Qn, preset, en
  J_K_Flip_Flop j_k_ff_2 (.J(out_3[0]), .clk(in_1), .K(out_3[0]), .Q(out_3[1]), .reset(Clear));  // open: Qn, preset, en
  and and_1 (and_1_out, out_3[0], out_3[1]);
  and and_2 (and_2_out, and_1_out, j_k_ff_5_qn, out_3[2]);
  J_K_Flip_Flop j_k_ff_3 (
    .J(and_1_out), .clk(in_1), .K(and_1_out), .Q(out_3[2]), .reset(Clear));  // open: Qn, preset, en
  J_K_Flip_Flop j_k_ff_4 (
    .J(and_2_out), .clk(in_1), .K(and_2_out), .Q(out_3[3]), .reset(Clear));  // open: Qn, preset, en
  xor xor_1 (xor_1_out, out_3[3], out_3[4]);
  and and_3 (and_3_out, and_1_out, out_3[2], xor_1_out);
  J_K_Flip_Flop j_k_ff_5 (
    .J(and_3_out), .clk(in_1), .K(and_3_out), .Q(out_3[4]), .Qn(j_k_ff_5_qn), .reset(Clear));  // open: preset, en
endmodule

module HHMMSS (
  output [4:0] HOUR
);

  wire and_1_out, and_2_out, Clear_out, clock_1_out, not_1_out, not_2_out, not_3_out, not_4_out, not_5_out,
       not_6_out, not_7_out, not_8_out;
  wire [3:0] MM_t, MM_z, SS_t, SS_z;

  Clock clock_1 (.out(clock_1_out));
  Button Clear (.out(Clear_out));
  s SS (.in_1(clock_1_out), .in_2(Clear_out), .Z(SS_z), .T(SS_t));
  not not_1 (not_1_out, SS_t[0]);
  not not_2 (not_2_out, SS_t[1]);
  not not_3 (not_3_out, SS_t[2]);
  not not_4 (not_4_out, SS_t[3]);
  Hex_Digit_Display hex_digit_display_1 ();  // open: value, dp
  and and_1 (and_1_out, not_1_out, not_2_out, not_3_out, not_4_out);
  Hex_Digit_Display hex_digit_display_2 (.value(MM_z));  // open: dp
  Hex_Digit_Display hex_digit_display_3 (.value(MM_t));  // open: dp
  s MM (.in_1(and_1_out), .in_2(Clear_out), .Z(MM_z), .T(MM_t));
  Hex_Digit_Display hex_digit_display_4 ();  // open: value, dp
  not not_5 (not_5_out, MM_t[0]);
  not not_6 (not_6_out, MM_t[1]);
  not not_7 (not_7_out, MM_t[2]);
  not not_8 (not_8_out, MM_t[3]);
  Hex_Digit_Display hex_digit_display_5 (.value(SS_z));  // open: dp
  Hex_Digit_Display hex_digit_display_6 (.value(SS_t));  // open: dp
  and and_2 (and_2_out, not_5_out, not_6_out, not_7_out, not_8_out);
  counter24 HH (.in_1(and_2_out), .Clear(Clear_out), .out_3(HOUR));

  // Notes on the sheet:
  //   MINUTES
  //   SECONDS
endmodule
