// Logisim project bcd_to_decimal.circ as structural Verilog: 1 circuit, main circuit main
module main (
  input  B0,
  input  B1,
  input  B2,
  input  B3,
  output out_5,
  output out_6,
  output out_7,
  output out_8,
  output out_9,
  output out_10,
  output out_11,
  output out_12,
  output out_13,
  output out_14
);

  wire not_1_out, not_2_out, not_3_out, not_4_out;

  not not_1 (not_1_out, B0);
  not not_2 (not_2_out, B1);
  not not_3 (not_3_out, B2);
  not not_4 (not_4_out, B3);
  and D0 (out_5, not_4_out, not_3_out, not_2_out, not_1_out);
  and D1 (out_6, not_4_out, not_3_out, not_2_out, B0);
  and D2 (out_7, B1, not_1_out, not_3_out);
  and D3 (out_8, B1, B0, not_3_out);
  and D4 (out_9, not_1_out, not_2_out, B2);
  and D5 (out_10, B2, not_2_out, B0);
  and D6 (out_11, not_1_out, B1, B2);
  and D7 (out_12, B0, B1, B2);
  and D8 (out_13, B3, not_1_out);
  and D9 (out_14, B3, B0);
endmodule
