// Logisim project cascade_decade.circ as structural Verilog: 2 circuits, main circuit main
module main (
  input  S,
  input  clr
);

  wire and_1_out, and_2_out, clk_out, multiplexer_1_out, not_1_out, not_2_out, not_3_out, not_4_out;
  wire [3:0] decade_1_out_4, decade_2_out_4;

  Clock clk (.out(clk_out));
  Decade decade_1 (.clk(clk_out), .S(S), .clr(clr), .out_4(decade_1_out_4));
  not not_1 (not_1_out, decade_1_out_4[0]);
  not not_2 (not_2_out, decade_1_out_4[1]);
  not not_3 (not_3_out, decade_1_out_4[2]);
  not not_4 (not_4_out, decade_1_out_4[3]);
  and and_1 (and_1_out, not_1_out, not_2_out, not_3_out, not_4_out);
  and and_2 (and_2_out, decade_1_out_4[3], decade_1_out_4[0]);
  Hex_Digit_Display hex_digit_display_1 (.value(decade_2_out_4));  // open: dp
  Multiplexer #(.enable("false")) multiplexer_1 (.in0(and_1_out), .in1(and_2_out), .out(multiplexer_1_out), .sel(S));
  Hex_Digit_Display hex_digit_display_2 (.value(decade_1_out_4));  // open: dp
  Decade decade_2 (.clk(multiplexer_1_out), .S(S), .clr(clr), .out_4(decade_2_out_4));
endmodule

// DECADE
module Decade (
  input  clk,
  input  S,
  input  clr,
  output [3:0] out_4
);

  wire and_1_out, and_2_out, and_3_out, and_4_out, and_5_out, and_6_out, and_7_out, and_8_out, and_9_out,
       and_10_out, and_11_out, j_k_ff_1_qn, j_k_ff_2_qn, j_k_ff_3_qn, j_k_ff_4_qn, multiplexer_1_out,
       multiplexer_2_out, multiplexer_3_out, or_1_out, or_2_out, or_3_out;

  J_K_Flip_Flop j_k_ff_1 (
    .J(1'b1), .clk(clk), .K(1'b1), .Q(out_4[0]), .Qn(j_k_ff_1_qn), .reset(clr));  // open: preset, en
  and and_1 (and_1_out, out_4[0], j_k_ff_4_qn);
  and and_2 (and_2_out, out_4[1], j_k_ff_1_qn);
  and and_3 (and_3_out, out_4[2], j_k_ff_1_qn);
  and and_4 (and_4_out, out_4[3], j_k_ff_1_qn);
  or or_1 (or_1_out, and_2_out, and_3_out, and_4_out);
  J_K_Flip_Flop j_k_ff_2 (
    .J(multiplexer_1_out), .clk(clk), .K(multiplexer_1_out), .Q(out_4[1]), .Qn(j_k_ff_2_qn), .reset(clr));  // open: preset, en
  Multiplexer #(.enable("false")) multiplexer_1 (.in0(and_1_out), .in1(or_1_out), .out(multiplexer_1_out), .sel(S));
  and and_5 (and_5_out, out_4[0], out_4[1]);
  and and_6 (and_6_out, j_k_ff_2_qn, j_k_ff_1_qn);
  and and_7 (and_7_out, out_4[2], and_6_out);
  and and_8 (and_8_out, and_6_out, out_4[3]);
  Multiplexer #(.enable("false")) multiplexer_2 (.in0(and_5_out), .in1(or_2_out), .out(multiplexer_2_out), .sel(S));
  or or_2 (or_2_out, and_7_out, and_8_out);
  J_K_Flip_Flop j_k_ff_3 (
    .J(multiplexer_2_out), .clk(clk), .K(multiplexer_2_out), .Q(out_4[2]), .Qn(j_k_ff_3_qn), .reset(clr));  // open: preset, en
  and and_9 (and_9_out, and_5_out, out_4[2]);
  or or_3 (or_3_out, and_9_out, and_10_out);
  and and_10 (and_10_out, out_4[0], out_4[3]);
  Multiplexer #(.enable("false")) multiplexer_3 (.in0(or_3_out), .in1(and_11_out), .out(multiplexer_3_out), .sel(S));
  and and_11 (and_11_out, j_k_ff_3_qn, j_k_ff_2_qn, j_k_ff_1_qn);
  J_K_Flip_Flop j_k_ff_4 (
    .J(multiplexer_3_out), .clk(clk), .K(multiplexer_3_out), .Q(out_4[3]), .Qn(j_k_ff_4_qn), .reset(clr));  // open: preset, en
endmodule
