// Logisim project digital_clock.circ as structural Verilog: 8 circuits, main circuit Mod 10 Counter
module Main_Clock_Circuit (
  input  Input_Enable,
  input  [3:0] Bit_5,
  input  [3:0] Bit_4,
  input  [3:0] Bit_1,
  input  [3:0] Bit_0,
  input  [3:0] Bit_3,
  input  [3:0] Bit_2
);

  wire and_1_out, CLEAR_out, CLOCK_out, Mod_60_Counter_2_clock_out, Mod_60_Counter_clock_out;
  wire [3:0] mod_24_counter_1_output_0, mod_24_counter_1_output_1, Mod_60_Counter_2_output_0,
       Mod_60_Counter_2_output_1, Mod_60_Counter_output_0, Mod_60_Counter_output_1;

  Clock CLOCK (.out(CLOCK_out));
  Button CLEAR (.out(CLEAR_out));
  and and_1 (and_1_out, CLEAR_out, Input_Enable);
  Mod_60_Counter Mod_60_Counter (
    .Clock(CLOCK_out), .Clear(CLEAR_out), .Input_Enable(and_1_out), .Parallel_Input_1(Bit_1),
    .Parallel_Input_0(Bit_0), .Output_1(Mod_60_Counter_output_1), .Output_0(Mod_60_Counter_output_0),
    .Clock_Out(Mod_60_Counter_clock_out));
  Hex_Digit_Display hex_digit_display_1 (.value(mod_24_counter_1_output_1));  // open: dp
  Hex_Digit_Display hex_digit_display_2 (.value(mod_24_counter_1_output_0));  // open: dp
  Hex_Digit_Display hex_digit_display_3 (.value(Mod_60_Counter_2_output_1));  // open: dp
  Hex_Digit_Display hex_digit_display_4 (.value(Mod_60_Counter_2_output_0));  // open: dp
  Mod_60_Counter Mod_60_Counter_2 (
    .Clock(Mod_60_Counter_clock_out), .Clear(CLEAR_out), .Input_Enable(and_1_out), .Parallel_Input_1(Bit_3),
    .Parallel_Input_0(Bit_2), .Output_1(Mod_60_Counter_2_output_1), .Output_0(Mod_60_Counter_2_output_0),
    .Clock_Out(Mod_60_Counter_2_clock_out));
  Hex_Digit_Display hex_digit_display_5 (.value(Mod_60_Counter_output_0));  // open: dp
  Hex_Digit_Display hex_digit_display_6 (.value(Mod_60_Counter_output_1));  // open: dp
  Mod_24_Counter mod_24_counter_1 (
    .Clear(CLEAR_out), .Clock(Mod_60_Counter_2_clock_out), .Input_Enable(and_1_out),
    .Parallel_Input_1(Bit_5), .Parallel_Input_0(Bit_4), .Output_1(mod_24_counter_1_output_1),
    .Output_0(mod_24_counter_1_output_0));

  // Notes on the sheet:
  //   Second's Input
  //   HOURS
  //   --
  //   MINUTES
  //   Minute's Input
  //   Digital Clock (HH:MM:SS)
  //   --
  //   SECONDS
  //   Hour's Input
endmodule

module Mod_60_Counter (
  input  Clock,
  input  Clear,
  input  Input_Enable,
  input  [3:0] Parallel_Input_1,
  input  [3:0] Parallel_Input_0,
  output [3:0] Output_1,
  output [3:0] Output_0,
  output Clock_Out
);

  wire Logic_Circuit_output;

  Mod_10_Counter Mod_10_Counter (
    .Clock(Clock), .Clear(Clear), .Input_Enable(Input_Enable), .Parallel_Input(Parallel_Input_0),
    .Output(Output_0));
  Logic_Circuit Logic_Circuit (.Input(Output_0), .Output(Logic_Circuit_output));
  Mod_6_Counter MOD_6_Counter (
    .Clock(Logic_Circuit_output), .Clear(Clear), .Input_Enable(Input_Enable),
    .Parallel_Input(Parallel_Input_1), .Output(Output_1));
  Logic_Circuit Clock_Out_Logic (.Input(Output_1), .Output(Clock_Out));

  // Notes on the sheet:
  //   MOD-60 Counter
endmodule

module Mod_24_Counter (
  input  Clear,
  input  Clock,
  input  Input_Enable,
  input  [3:0] Parallel_Input_1,
  input  [3:0] Parallel_Input_0,
  output [3:0] Output_1,
  output [3:0] Output_0
);

  wire Clear_Generator_output, Logic_Circuit_output, or_1_out;

  or or_1 (or_1_out, Clear, Clear_Generator_output);
  Mod_10_Counter Mod_10_Counter (
    .Clock(Clock), .Clear(or_1_out), .Input_Enable(Input_Enable), .Parallel_Input(Parallel_Input_0),
    .Output(Output_0));
  Logic_Circuit Logic_Circuit (.Input(Output_0), .Output(Logic_Circuit_output));
  Clear_Generator Clear_Generator (.Output(Clear_Generator_output), .Input_1(Output_1), .Input_0(Output_0));
  Mod_3_Counter Mod_3_Counter (
    .Clock(Logic_Circuit_output), .Clear(or_1_out), .Input_Enable(Input_Enable),
    .Parallel_Input(Parallel_Input_1), .Output(Output_1));

  // Notes on the sheet:
  //   MOD-24 Counter
endmodule

module Mod_10_Counter (
  input  Clock,
  input  Clear,
  input  Input_Enable,
  input  [3:0] Parallel_Input,
  output [3:0] Output
);

  wire and_1_out, and_2_out, and_3_out, and_4_out, and_5_out, and_6_out, and_7_out, and_8_out, j_k_ff_4_qn,
       or_1_out;

  and and_1 (and_1_out, Input_Enable, Parallel_Input[0]);
  and and_2 (and_2_out, Output[0], j_k_ff_4_qn);
  J_K_Flip_Flop j_k_ff_1 (
    .J(1'b1), .clk(Clock), .K(1'b1), .Q(Output[0]), .preset(and_1_out), .reset(Clear));  // open: Qn, en
  J_K_Flip_Flop j_k_ff_2 (
    .J(and_2_out), .clk(Clock), .K(and_2_out), .Q(Output[1]), .preset(and_3_out), .reset(Clear));  // open: Qn, en
  and and_3 (and_3_out, Input_Enable, Parallel_Input[1]);
  and and_4 (and_4_out, Output[0], Output[1]);
  J_K_Flip_Flop j_k_ff_3 (
    .J(and_4_out), .clk(Clock), .K(and_4_out), .Q(Output[2]), .preset(and_5_out), .reset(Clear));  // open: Qn, en
  and and_5 (and_5_out, Input_Enable, Parallel_Input[2]);
  and and_6 (and_6_out, and_4_out, Output[2]);
  or or_1 (or_1_out, and_6_out, and_7_out);
  and and_7 (and_7_out, Output[0], Output[3]);
  J_K_Flip_Flop j_k_ff_4 (
    .J(or_1_out), .clk(Clock), .K(or_1_out), .Q(Output[3]), .Qn(j_k_ff_4_qn), .preset(and_8_out),
    .reset(Clear));  // open: en
  and and_8 (and_8_out, Input_Enable, Parallel_Input[3]);

  // Notes on the sheet:
  //   MOD-10 Counter
endmodule

module Mod_6_Counter (
  input  Clock,
  input  Clear,
  input  Input_Enable,
  input  [3:0] Parallel_Input,
  output [3:0] Output
);

  wire and_1_out, and_2_out, and_3_out, and_4_out, and_5_out, and_6_out, j_k_ff_3_qn, or_1_out;

  and and_1 (and_1_out, Input_Enable, Parallel_Input[0]);
  J_K_Flip_Flop j_k_ff_1 (
    .J(1'b1), .clk(Clock), .K(1'b1), .Q(Output[0]), .preset(and_1_out), .reset(Clear));  // open: Qn, en
  and and_2 (and_2_out, j_k_ff_3_qn, Output[0]);
  J_K_Flip_Flop j_k_ff_2 (
    .J(and_2_out), .clk(Clock), .K(and_2_out), .Q(Output[1]), .preset(and_3_out), .reset(Clear));  // open: Qn, en
  and and_3 (and_3_out, Input_Enable, Parallel_Input[1]);
  and and_4 (and_4_out, Output[2], Output[0]);
  and and_5 (and_5_out, Output[0], Output[1]);
  or or_1 (or_1_out, and_4_out, and_5_out);
  and and_6 (and_6_out, Input_Enable, Parallel_Input[2]);
  J_K_Flip_Flop j_k_ff_3 (
    .J(or_1_out), .clk(Clock), .K(or_1_out), .Q(Output[2]), .Qn(j_k_ff_3_qn), .preset(and_6_out),
    .reset(Clear));  // open: en

  assign Output[3] = 1'b0;
  // also tied to GND on the sheet: Parallel_Input[3]

  // Notes on the sheet:
  //   MOD-6 Counter
endmodule

module Mod_3_Counter (
  input  Clock,
  input  Clear,
  input  Input_Enable,
  input  [3:0] Parallel_Input,
  output [3:0] Output
);

  wire and_1_out, and_2_out, j_k_ff_1_qn;

  J_K_Flip_Flop j_k_ff_1 (
    .J(Output[0]), .clk(Clock), .K(1'b1), .Q(Output[1]), .Qn(j_k_ff_1_qn), .preset(and_1_out), .reset(Clear));  // open: en
  and and_1 (and_1_out, Input_Enable, Parallel_Input[1]);
  J_K_Flip_Flop j_k_ff_2 (
    .J(j_k_ff_1_qn), .clk(Clock), .K(1'b1), .Q(Output[0]), .preset(and_2_out), .reset(Clear));  // open: Qn, en
  and and_2 (and_2_out, Input_Enable, Parallel_Input[0]);

  assign Output[3:2] = 2'b00;
  assign Parallel_Input[2] = Parallel_Input[3];
  // also tied to GND on the sheet: Parallel_Input[3]

  // Notes on the sheet:
  //   MOD-3 Counter
endmodule

module Clear_Generator (
  input  [3:0] Input_1,
  input  [3:0] Input_0,
  output Output
);

  wire and_2_out, and_3_out, not_1_out, not_2_out, not_3_out, not_4_out, not_5_out, not_6_out;

  and and_1 (Output, and_2_out, and_3_out);
  and and_2 (and_2_out, not_1_out, Input_1[1], not_2_out, not_3_out);
  and and_3 (and_3_out, not_4_out, not_5_out, Input_0[2], not_6_out);
  not not_1 (not_1_out, Input_1[0]);
  not not_2 (not_2_out, Input_1[2]);
  not not_3 (not_3_out, Input_1[3]);
  not not_4 (not_4_out, Input_0[0]);
  not not_5 (not_5_out, Input_0[1]);
  not not_6 (not_6_out, Input_0[3]);

  // Notes on the sheet:
  //   Clear Generator Circuit
endmodule

module Logic_Circuit (
  input  [3:0] Input,
  output Output
);

  wire not_1_out, not_2_out, not_3_out, not_4_out;

  not not_1 (not_1_out, Input[1]);
  not not_2 (not_2_out, Input[3]);
  not not_3 (not_3_out, Input[0]);
  not not_4 (not_4_out, Input[2]);
  and and_1 (Output, not_3_out, not_1_out, not_4_out, not_2_out);

  // Notes on the sheet:
  //   Logic Circuit
endmodule
