// Logisim project serial_adder.circ as structural Verilog: 7 circuits, main circuit main
module main (
  input  Shift_load,
  input  CLEAR,
  input  CLEAR_2,
  input  CLEAR_3,
  output [2:0] A,
  output out_6,
  output out_7,
  output [2:0] FINAL_SUM,
  output out_9,
  output out_10,
  output FINAL_CARRY,
  output [2:0] B
);

  wire clock_1_out, clock_2_out;

  Clock clock_1 (.out(clock_1_out));
  Clock clock_2 (.out(clock_2_out));
  COUNTER counter_1 (.CLOCK(clock_2_out), .CLEAR(CLEAR), .out_3(A));
  COUNTER counter_2 (.CLOCK(clock_2_out), .CLEAR(CLEAR_2), .out_3(B));
  PISO_REGISTER piso_register_1 (.SHIFT_LOAD(Shift_load), .CLK(clock_1_out), .CLEAR(CLEAR_3), .out_5(out_6), .in_1(A));
  PISO_REGISTER piso_register_2 (.SHIFT_LOAD(Shift_load), .CLK(clock_1_out), .CLEAR(CLEAR_3), .out_5(out_10), .in_1(B));
  FULL_ADDER full_adder_1 (.A(out_6), .B(out_10), .Cin(FINAL_CARRY), .CARRY(out_9), .SUM(out_7));
  D_Flip_Flop d_ff_1 (.clk(clock_1_out), .D(out_9), .Q(FINAL_CARRY));  // open: Qn, preset, en, reset
  SIPO_REGISTER sipo_register_1 (.CLK(clock_1_out), .in_2(out_7), .CLEAR(CLEAR_3), .out_4(FINAL_SUM));
endmodule

module COUNTER (
  input  CLOCK,
  input  CLEAR,
  output [2:0] out_3
);

  wire t_ff_1_q, t_ff_2_q;

  T_Flip_Flop t_ff_1 (.clk(CLOCK), .T(1'b1), .Q(t_ff_1_q), .Qn(out_3[0]), .reset(CLEAR));  // open: preset, en
  T_Flip_Flop t_ff_2 (.clk(t_ff_1_q), .T(1'b1), .Q(t_ff_2_q), .Qn(out_3[1]), .reset(CLEAR));  // open: preset, en
  T_Flip_Flop t_ff_3 (.clk(t_ff_2_q), .T(1'b1), .Qn(out_3[2]), .reset(CLEAR));  // open: Q, preset, en
endmodule

module OR (
  input  in_1,
  input  in_2,
  output out_3
);

  wire nand_1_out, nand_2_out;

  nand nand_1 (nand_1_out, in_1, in_1);
  nand nand_2 (nand_2_out, in_2, in_2);
  nand nand_3 (out_3, nand_1_out, nand_2_out);
endmodule

// HA
module HALF_ADDER (
  input  A,
  input  B,
  output Sum,
  output Carry
);

  wire nand_1_out, nand_2_out, nand_4_out;

  nand nand_1 (nand_1_out, A, B);
  nand nand_2 (nand_2_out, A, nand_1_out);
  nand nand_3 (Sum, nand_2_out, nand_4_out);
  nand nand_4 (nand_4_out, nand_1_out, B);
  nand nand_5 (Carry, nand_1_out, nand_1_out);
endmodule

// FA
module FULL_ADDER (
  input  A,
  input  B,
  input  Cin,
  output SUM,
  output CARRY
);

  wire half_adder_1_carry, half_adder_1_sum, half_adder_2_carry;

  HALF_ADDER half_adder_1 (.A(A), .B(B), .Sum(half_adder_1_sum), .Carry(half_adder_1_carry));
  HALF_ADDER half_adder_2 (.A(half_adder_1_sum), .B(Cin), .Sum(SUM), .Carry(half_adder_2_carry));
  OR or_1 (.in_1(half_adder_2_carry), .in_2(half_adder_1_carry), .out_3(CARRY));
endmodule

// PISO
module PISO_REGISTER (
  input  [2:0] in_1,
  input  SHIFT_LOAD,
  input  CLK,
  input  CLEAR,
  output out_5
);

  wire d_ff_1_q, d_ff_2_q, nand_1_out, nand_2_out, nand_3_out, nand_4_out, nand_5_out, nand_6_out, nand_7_out;

  nand nand_1 (nand_1_out, SHIFT_LOAD, SHIFT_LOAD);
  D_Flip_Flop d_ff_1 (.clk(CLK), .D(in_1[2]), .Q(d_ff_1_q), .reset(CLEAR));  // open: Qn, preset, en
  nand nand_2 (nand_2_out, d_ff_1_q, SHIFT_LOAD);
  nand nand_3 (nand_3_out, nand_1_out, in_1[1]);
  nand nand_4 (nand_4_out, nand_2_out, nand_3_out);
  D_Flip_Flop d_ff_2 (.clk(CLK), .D(nand_4_out), .Q(d_ff_2_q), .reset(CLEAR));  // open: Qn, preset, en
  nand nand_5 (nand_5_out, d_ff_2_q, SHIFT_LOAD);
  nand nand_6 (nand_6_out, nand_5_out, nand_7_out);
  nand nand_7 (nand_7_out, nand_1_out, in_1[0]);
  D_Flip_Flop d_ff_3 (.clk(CLK), .D(nand_6_out), .Q(out_5), .reset(CLEAR));  // open: Qn, preset, en
endmodule

// SIPO
module SIPO_REGISTER (
  input  CLK,
  input  in_2,
  input  CLEAR,
  output [2:0] out_4
);

  D_Flip_Flop d_ff_1 (.clk(CLK), .D(in_2), .Q(out_4[2]), .reset(CLEAR));  // open: Qn, preset, en
  D_Flip_Flop d_ff_2 (.clk(CLK), .D(out_4[2]), .Q(out_4[1]), .reset(CLEAR));  // open: Qn, preset, en
  D_Flip_Flop d_ff_3 (.clk(CLK), .D(out_4[1]), .Q(out_4[0]), .reset(CLEAR));  // open: Qn, preset, en
endmodule
