// Logisim project signed_adder.circ as structural Verilog: 8 circuits, main circuit main
module main (
  input  in_1,
  input  in_2,
  output [2:0] A_BEFORE_CHCEK,
  output [2:0] A,
  output [3:0] out_5,
  output [2:0] B_BEFORE_CHECK,
  output [2:0] B
);

  wire clock_1_out;

  Clock clock_1 (.out(clock_1_out));
  COUNTER counter_1 (.CLOCK(clock_1_out), .CLEAR(in_1), .out_3(A_BEFORE_CHCEK));
  COUNTER counter_2 (.CLOCK(clock_1_out), .CLEAR(in_2), .out_3(B_BEFORE_CHECK));
  CHECK check_1 (.INPUT_NUMBER(A_BEFORE_CHCEK), .POSITIVE_NUMBER(A));
  CHECK check_2 (.INPUT_NUMBER(B_BEFORE_CHECK), .POSITIVE_NUMBER(B));
  _3_bit_ADDER u_3_bit_adder_1 (.in_1(A), .in_2(B), .out_3(out_5));
endmodule

module COUNTER (
  input  CLOCK,
  input  CLEAR,
  output [2:0] out_3
);

  wire t_ff_1_q, t_ff_2_q;

  T_Flip_Flop t_ff_1 (.clk(CLOCK), .T(1'b1), .Q(t_ff_1_q), .Qn(out_3[0]), .reset(CLEAR));  // open: preset, en
  T_Flip_Flop t_ff_2 (.clk(t_ff_1_q), .T(1'b1), .Q(t_ff_2_q), .Qn(out_3[1]), .reset(CLEAR));  // open: preset, en
  T_Flip_Flop t_ff_3 (.clk(t_ff_2_q), .T(1'b1), .Qn(out_3[2]), .reset(CLEAR));  // open: Q, preset, en
endmodule

module OR (
  input  in_1,
  input  in_2,
  output out_3
);

  wire nand_1_out, nand_2_out;

  nand nand_1 (nand_1_out, in_1, in_1);
  nand nand_2 (nand_2_out, in_2, in_2);
  nand nand_3 (out_3, nand_1_out, nand_2_out);
endmodule

// HA
module HALF_ADDER (
  input  A,
  input  B,
  output Sum,
  output Carry
);

  wire nand_1_out, nand_2_out, nand_4_out;

  nand nand_1 (nand_1_out, A, B);
  nand nand_2 (nand_2_out, A, nand_1_out);
  nand nand_3 (Sum, nand_2_out, nand_4_out);
  nand nand_4 (nand_4_out, nand_1_out, B);
  nand nand_5 (Carry, nand_1_out, nand_1_out);
endmodule

module FULL_ADDER (
  input  A,
  input  B,
  input  Cin,
  output out_4,
  output out_5
);

  wire half_adder_1_carry, half_adder_1_sum, half_adder_2_carry;

  HALF_ADDER half_adder_1 (.A(A), .B(B), .Sum(half_adder_1_sum), .Carry(half_adder_1_carry));
  HALF_ADDER half_adder_2 (.A(half_adder_1_sum), .B(Cin), .Sum(out_5), .Carry(half_adder_2_carry));
  OR or_1 (.in_1(half_adder_2_carry), .in_2(half_adder_1_carry), .out_3(out_4));
endmodule

// ADDER
module _3_bit_ADDER (
  input  [2:0] in_1,
  input  [2:0] in_2,
  output [3:0] out_3
);

  wire full_adder_1_out_4, half_adder_1_carry;

  HALF_ADDER half_adder_1 (.A(in_1[0]), .B(in_2[0]), .Sum(out_3[0]), .Carry(half_adder_1_carry));
  FULL_ADDER full_adder_1 (
    .A(in_1[1]), .B(in_2[1]), .Cin(half_adder_1_carry), .out_4(full_adder_1_out_4), .out_5(out_3[1]));
  FULL_ADDER full_adder_2 (.A(in_1[2]), .B(in_2[2]), .Cin(full_adder_1_out_4), .out_4(out_3[3]), .out_5(out_3[2]));
endmodule

module CHECK (
  input  [2:0] INPUT_NUMBER,
  output [2:0] POSITIVE_NUMBER
);

  wire LSB_2_carry, LSB_xor, NEXT_TO_MSB_2_carry, Next_to_MSB_xor;

  XOR Next_to_MSB (.XOR(Next_to_MSB_xor), .in_1(INPUT_NUMBER[1]), .in_2(INPUT_NUMBER[2]));
  XOR LSB (.XOR(LSB_xor), .in_1(INPUT_NUMBER[0]), .in_2(INPUT_NUMBER[2]));
  HALF_ADDER LSB_2 (.A(LSB_xor), .B(INPUT_NUMBER[2]), .Sum(POSITIVE_NUMBER[0]), .Carry(LSB_2_carry));
  HALF_ADDER MSB (.A(INPUT_NUMBER[2]), .B(NEXT_TO_MSB_2_carry), .Sum(POSITIVE_NUMBER[2]));  // open: Carry
  HALF_ADDER NEXT_TO_MSB_2 (
    .A(Next_to_MSB_xor), .B(LSB_2_carry), .Sum(POSITIVE_NUMBER[1]), .Carry(NEXT_TO_MSB_2_carry));
endmodule

module XOR (
  input  in_1,
  input  in_2,
  output XOR
);

  wire nand_1_out, nand_2_out, nand_3_out;

  nand nand_1 (nand_1_out, in_1, in_2);
  nand nand_2 (nand_2_out, in_1, nand_1_out);
  nand nand_3 (nand_3_out, nand_1_out, in_2);
  nand nand_4 (XOR, nand_2_out, nand_3_out);
endmodule
